# Fritzing sketch trinket2lora (saved by Fritzing 0.9.3b)
breadboards: 1

parts:
  Part1 = Adafruit RFM9x LoRa Radio [part_number="Adafruit #3072 and #3073"]
  Part2 = Adafruit Pro Trinket 3.3V 12MHz [part_number="Adafruit #2010"]

nets:
  VIN: Part1.VIN, Part2.+3V3
  GND: Part1.GND, Part2.GND
  N1: Part1.DIO0, Part2.D3
  N2: Part1.SCK, Part2.D13
  N3: Part1.MOSI, Part2.D11
  N4: Part1.CS, Part2.D4
  N5: Part1.RST, Part2.D5

custom parts:
  Adafruit RFM9x LoRa Radio: Sending data over long distances is like magic, and now you can be a magician with this range of powerful and easy-to-use radio modules. Sure, sometimes you want to talk to a computer (a good time to use WiFi) or perhaps communicate with a Phone (choose Bluetooth Low Energy!) but what if you want to send data very far? Most WiFi, Bluetooth, Zigbee and other wireless chipsets use 2.4GHz, which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
  Adafruit Pro Trinket 3.3V 12MHz: rinket's got a big sister in town - the Pro Trinket 3V! Pro Trinket combines everything you love about Trinket with the familiarity of the core Arduino chip, the ATmega328. It's like an Arduino Pro Mini with more pins and USB tossed in. Trinket's a year old now, and while its been great to see tons of tiny projects, sometimes you just need more pins, more FLASH, and more RAM. That's why we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
